# Fritzing sketch schema_due_display_7_segmenti-esp4 (saved by Fritzing 0.9.3b)
breadboards: 1

parts:
  Componente1 = Arduino Board Ethernet
  7_Segment1 = 7 Segment Display
  7_Segment2 = 7 Segment Display
  R1 = Resistor [tolerance=±5% resistance=220 package=THT]
  R2 = Resistor [tolerance=±5% resistance=220 package=THT]

nets:
  N1: Componente1.D8, 7_Segment1.Segment_F, 7_Segment2.Segment_F
  N2: Componente1.D9_PWM, 7_Segment1.Segment_A, 7_Segment2.Segment_A
  N3: Componente1.D10_PWM/SS, 7_Segment1.Segment_B, 7_Segment2.Segment_B
  N4: Componente1.D2_PWM, R2.Pin_1
  N5: Componente1.D3_PWM, R1.Pin_1
  N6: Componente1.D4, 7_Segment1.Segment_C, 7_Segment2.Segment_C
  N7: Componente1.D5_PWM, 7_Segment1.Segment_D, 7_Segment2.Segment_D
  N8: Componente1.D6_PWM, 7_Segment1.Segment_E, 7_Segment2.Segment_E
  N9: Componente1.D7, 7_Segment1.Segment_G, 7_Segment2.Segment_G
  N10: 7_Segment1.common_anode, R1.Pin_0
  N11: 7_Segment2.common_anode, R2.Pin_0
